// Logisim project PcSrc.circ as structural Verilog: 1 circuit, main circuit main
module main (
  input  [4:0] in_1,
  output [1:0] PcSrc
);

  wire decoder_1_out6, decoder_1_out11, decoder_1_out12, decoder_1_out13;

  Decoder #(.select(5), .enable("false")) decoder_1 (
    .out6(decoder_1_out6), .out11(decoder_1_out11), .out12(decoder_1_out12), .out13(decoder_1_out13),
    .sel(in_1));  // open: out0, out1, out2, out3, out4, out5, out7, out8, out9, out10, out14, out15, out16, out17, out18, out19, out20, out21, out22, out23, out24, out25, out26, out27, out28, out29, out30, out31
  or or_1 (PcSrc[1], decoder_1_out11, decoder_1_out12, decoder_1_out13);
  nor nor_1 (PcSrc[0], decoder_1_out6, decoder_1_out12, decoder_1_out13);
endmodule
